# Fritzing sketch Moisture-perfboard (saved by Fritzing 0.9.3b)
circuit board: 8.46667cm x 5.64444cm
perfboards: 2

parts:
  Composant1 = Arduino MKR1000
  Capacitive_Soil_Moisture_Sensor1 = DFRobot Capacitive Soil Moisture Sensor V1.0 [part_number=SEN0193]
  M1 = DC Motor
  R1 = Resistor [tolerance=±5% resistance=1k package=THT]
  R2 = Resistor [tolerance=±5% resistance=10k package=THT]
  R3 = Resistor [tolerance=±5% resistance=4.7k package=THT]
  Q1 = NPN-Transistor [package="TO92 [THT]"]
  L1 = Inductor [package="400 mil [THT]"]  # not connected
  C1 = Ceramic Capacitor [capacitance=100nF package="100 mil [THT, multilayer]"]
  KY-1 = Keyes Relay [package=THT]
  LCD1 = LCD screen
  C2 = Ceramic Capacitor [capacitance=100nF package="100 mil [THT, multilayer]"]
  JACK1 = 2.1mm Barrel Jack with Terminal Block
  JP4 = Header 3 [package=screwterminal-3.5mm-3_lock.007s]

nets:
  N1: Composant1.A1, Capacitive_Soil_Moisture_Sensor1.A, JP4.3
  N2: Composant1.D0, LCD1.V0
  N3: Composant1.D1, LCD1.RS
  N4: Composant1.D2_PWM, LCD1.E
  N5: Composant1.D3_PWM, LCD1.DB4
  N6: Composant1.D4_PWM, LCD1.DB5
  N7: Composant1.D5_PWM, LCD1.DB6
  N8: Composant1.D6, LCD1.DB7
  N9: Composant1.D7, R1.Pin_1, R2.Pin_1
  VIN: Composant1.VIN, Capacitive_Soil_Moisture_Sensor1.VCC, KY-1.C, JP4.2
  N10: Capacitive_Soil_Moisture_Sensor1.GND, LCD1.R/W, JACK1.POS, JP4.1
  N11: M1.pin_1, M1.pin_2, C1.0, C2.0
  N12: R1.Pin_0, Q1.B
  N13: R3.Pin_0, Q1.C, KY-1.ground
  N14: R3.Pin_1, KY-1.signal
  N15: KY-1.NO, C2.1

custom parts:
  Arduino MKR1000: MKR1000 is a powerful board that combines the functionality of the Zero and the Wi-Fi Shield. It is the ideal solution for makers wanting to design IoT projects with minimal previous experience in networking
  DFRobot Capacitive Soil Moisture Sensor V1.0: DFRobot Capacitive Soil Moisture Sensor V1.0 This product measures soil moisture levels by capacitive sensing, rather than resistive sensing like other types of moisture sensor. It is made of a corrosion resistant material giving it a long service life. Insert it into soil and impress your friends with the real-time soil moisture data! The product includes an on-board voltage regulator which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
  Keyes Relay: The Keyes 5V relay module is suitable for SCM development, home appliance control. It uses a 5V~12V TIL control signal which can control DC / AC signal.
