# Fritzing sketch Moisture-simple (saved by Fritzing 0.9.3b)
breadboards: 1

parts:
  Composant1 = Arduino MKR1000
  LCD1 = LCD screen
  Capacitive_Soil_Moisture_Sensor1 = DFRobot Capacitive Soil Moisture Sensor V1.0 [part_number=SEN0193]
  M1 = DC Motor
  KY-1 = Keyes Relay [package=THT]
  JACK1 = 2.1mm Barrel Jack with Terminal Block

nets:
  N1: Composant1.A1, Capacitive_Soil_Moisture_Sensor1.A
  N2: Composant1.D0, LCD1.RS
  N3: Composant1.D1, LCD1.E
  N4: Composant1.D2_PWM, LCD1.DB4
  N5: Composant1.D3_PWM, LCD1.DB5
  N6: Composant1.D4_PWM, LCD1.DB6
  N7: Composant1.D5_PWM, LCD1.DB7
  N8: Composant1.D6, LCD1.V0
  N9: Composant1.D7, KY-1.signal
  GND: Composant1.GND, LCD1.VSS, LCD1.R/W, Capacitive_Soil_Moisture_Sensor1.GND, KY-1.ground, KY-1.C, JACK1.POS
  N10: Composant1.VIN, M1.pin_1, JACK1.NEG
  5V: Composant1.5V, LCD1.VDD, Capacitive_Soil_Moisture_Sensor1.VCC, KY-1.power
  N11: M1.pin_2, KY-1.NO

custom parts:
  Arduino MKR1000: MKR1000 is a powerful board that combines the functionality of the Zero and the Wi-Fi Shield. It is the ideal solution for makers wanting to design IoT projects with minimal previous experience in networking
  DFRobot Capacitive Soil Moisture Sensor V1.0: DFRobot Capacitive Soil Moisture Sensor V1.0 This product measures soil moisture levels by capacitive sensing, rather than resistive sensing like other types of moisture sensor. It is made of a corrosion resistant material giving it a long service life. Insert it into soil and impress your friends with the real-time soil moisture data! The product includes an on-board voltage regulator which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
  Keyes Relay: The Keyes 5V relay module is suitable for SCM development, home appliance control. It uses a 5V~12V TIL control signal which can control DC / AC signal.
